# Fritzing sketch scheme (saved by Fritzing 0.9.3b)

parts:
  U1 = LIPO-1000mAh [package=lipo-1000]
  U2 = LIPO-1000mAh [package=lipo-1000]
  U3 = LIPO-1000mAh [package=lipo-1000]
  J3 = female pin header, 6 pins [form="♀ (female)"]
  U4 = ESP8266 WiFi Module [part_number=ESP8266]
  Часть1 = InvenSense MPU6050
  J4 = Basic Servo
  J5 = Basic Servo
  J7 = Basic Servo
  J8 = female pin header, 3 pins [form="♀ (female)"]
  J9 = female pin header, 3 pins [form="♀ (female)"]
  J10 = female pin header, 3 pins [form="♀ (female)"]
  J11 = female pin header, 3 pins [form="♀ (female)"]
  J6 = Basic Servo
  Часть3 = Arduino Pro Mini v13
  U5 = DC-DC_CONVERTER [package=dc-dc_converter]
  J14 = female pin header, 2 pins [form="♀ (female)"]
  J15 = female pin header, 2 pins [form="♀ (female)"]
  R1 = Resistor [tolerance=±5% resistance=1k package=THT]
  R2 = Resistor [tolerance=±5% resistance=1k package=THT]

nets:
  N1: U1.+, J15.pin1
  N2: U1.-, U2.+
  N3: U2.-, U3.+
  N4: U3.-, J15.pin2
  N5: J3.pin2, J14.pin1
  N6: J3.pin3, Часть3.D9_PWM
  N7: J3.pin4, Часть3.D6_PWM
  N8: J3.pin5, Часть3.D5_PWM
  N9: J3.pin6, Часть3.D3_PWM
  N10: U4.RXD, Часть3.D7
  N11: U4.VCC, U5.ON_OFF, R1.Pin_1
  N12: U4.GND, U5.VOUT, R2.Pin_0
  N13: U4.TXD, Часть3.D8
  N14: U4.GPIO_15, R2.Pin_1
  N15: U4.ADC_0, R1.Pin_0
  VCC: Часть1.VCC, Часть3.VCC
  N16: Часть1.SCL, Часть3.A5
  N17: Часть1.SDA, Часть3.A4
  N18: J4.gnd, J11.pin1
  N19: J4.vcc, J11.pin2
  N20: J4.pulse, J11.pin3
  N21: J5.gnd, J10.pin1
  N22: J5.vcc, J10.pin2
  N23: J5.pulse, J10.pin3
  N24: J7.gnd, J9.pin1
  N25: J7.vcc, J9.pin2
  N26: J7.pulse, J9.pin3
  N27: J8.pin1, J6.gnd
  N28: J8.pin2, J6.vcc
  N29: J8.pin3, J6.pulse
  N30: Часть3.RAW, U5.VIN
  N31: Часть3.GND, U5.SENSE
  N32: U5.SEQ, J14.pin2

notes:
  3S 1P 500mah
  4x (1104 7500KV 2-3S Motor)
  MPU-6050
  SCL ->A5
  SDA -> A4
  11.1V -> 3.3V
  ESP-07
